# Fritzing sketch nao_durma_no_transito (saved by Fritzing 0.9.3b)
breadboards: 1

parts:
  Componente5 = Arduino Uno (Rev3)
  J2 = Piezo Speaker
  GY1 = MPU-6050 Board GY-521 [form="♀ (female)" package=THT]

nets:
  N1: Componente5.A4/SDA, GY1.pin4
  N2: Componente5.A5/SCL, GY1.pin3
  N3: Componente5.D9_PWM, J2.pin2
  N4: Componente5.5V, GY1.pin1
  N5: Componente5.GND, J2.pin1, GY1.pin2

custom parts:
  MPU-6050 Board GY-521: Acelerometro y Giroscopio MPU-6050 Board GY-521

// code stored in the sketch: Untitled3.ino

